# Fritzing sketch PlantWater (saved by Fritzing 0.9.4)
breadboards: 1

parts:
  Argon1 = Particle Argon
  OLED_I2C1 = OLED 128x64 I2C Monochrome Display
  Part1 = BME280 Breakout  # not connected
  R1 = Resistor [tolerance=±5% resistance=220 package=THT]
  Q1 = PNP-Transistor [package="TO92 [THT]"]
  R2 = Resistor [tolerance=±5% resistance=220 package=THT]
  Part2 = MQ-131 breakout
  Grove1 = Grove Dust Sensor
  M1 = DC Motor
  Relay1 = Relay - 6 pins [package="DIP (Dual Inline) [THT]"]
  Chirp!_Soil_Moisture_Sensor1 = Chirp! Soil Moisture Sensor v2.7.3

nets:
  3.3V: Argon1.3.3V, Relay1.VCC
  GND: Argon1.GND, Q1.C, R2.Pin_0, M1.pin_2, Relay1.GND
  N1: Argon1.A0, Grove1.SIG
  N2: Argon1.A1, Part2.DO
  N3: Argon1.A2, Chirp!_Soil_Moisture_Sensor1.pin_3
  N4: Argon1.MI, Q1.B, R2.Pin_1
  N5: Argon1.SDA, OLED_I2C1.SDA
  N6: Argon1.SCL, OLED_I2C1.SCK
  VCC: OLED_I2C1.VDD, R1.Pin_0, Part2.VCC, Grove1.VCC, Chirp!_Soil_Moisture_Sensor1.Pin_1
  N7: R1.Pin_1, Q1.E, Relay1.IN
  GND_2: Part2.GND, Grove1.GND, Chirp!_Soil_Moisture_Sensor1.pin_5
  N8: M1.pin_1, Relay1.COM

custom parts:
  Particle Argon: The Argon is a powerful Wi-Fi enabled development board that can act as either a standalone Wi-Fi endpoint or Wi-Fi enabled gateway for Particle Mesh networks. It is based on the Nordic nRF52840 and has built-in battery charging circuitry so it’s easy to connect a Li-Po and deploy your local network in minutes. The Argon is great for connecting existing projects to the Particle Device Cloud or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
  MQ-131 breakout: SKU: 101282
  Grove Dust Sensor: PPD42 Grove Dust Sensor
  Relay - 6 pins: A DIP stand-in part for whatever IC you want. With 6 pins on a 900mil dual inline package (DIP) footprint.
